// Logisim project SUB_ADD_MOTOR.circ as structural Verilog: 7 circuits, main circuit main
module main (
  input  [3:0] A,
  input  [3:0] B,
  output [3:0] S,
  output [3:0] S_2
);

  add_4 add_4_1 (.A(A), .B(B), .S(S));  // open: out_3
  sub_4 sub_4_1 (.A(A), .B(B), .out_4(S_2));  // open: Overflow
endmodule

module Acionamento (
  input  A,
  input  B,
  input  C___Sensor_IR,
  output Lampada,
  output Motor
);

  or or_1 (Lampada, B, A);
  and and_1 (Motor, Lampada, C___Sensor_IR);
endmodule

module sub_1 (
  input  A,
  input  B,
  input  C,
  output S,
  output VAI_1
);

  wire and_1_out, and_2_out, or_1_out, xor_1_out;

  xor xor_1 (xor_1_out, A, B);
  or or_1 (or_1_out, B, C);
  xor xor_2 (S, xor_1_out, C);
  and and_1 (and_1_out, or_1_out, ~A);  // AND_Gate
  and and_2 (and_2_out, B, C);
  or or_2 (VAI_1, and_1_out, and_2_out);
endmodule

module sub_4 (
  input  [3:0] B,
  input  [3:0] A,
  output Overflow,
  output [3:0] out_4
);

  wire sub_1_2_vai_1, sub_1_3_vai_1, sub_1_4_vai_1;

  sub_1 sub_1_1 (.VAI_1(Overflow), .A(A[3]), .B(B[3]), .C(sub_1_3_vai_1), .S(out_4[3]));
  sub_1 sub_1_2 (.VAI_1(sub_1_2_vai_1), .A(A[1]), .B(B[1]), .C(sub_1_4_vai_1), .S(out_4[1]));
  sub_1 sub_1_3 (.VAI_1(sub_1_3_vai_1), .A(A[2]), .B(B[2]), .C(sub_1_2_vai_1), .S(out_4[2]));
  sub_1 sub_1_4 (.VAI_1(sub_1_4_vai_1), .A(A[0]), .B(B[0]), .C(1'b0), .S(out_4[0]));
endmodule

module add_4 (
  input  [3:0] B,
  input  [3:0] A,
  output out_3,
  output [3:0] S
);

  wire add_1_2_out_4, add_1_3_out_4, add_1_4_out_4;

  add_1 add_1_1 (.A(A[3]), .B(B[3]), .C(add_1_3_out_4), .out_4(out_3), .out_5(S[3]));
  add_1 add_1_2 (.A(A[1]), .B(B[1]), .C(add_1_4_out_4), .out_4(add_1_2_out_4), .out_5(S[1]));
  add_1 add_1_3 (.A(A[2]), .B(B[2]), .C(add_1_2_out_4), .out_4(add_1_3_out_4), .out_5(S[2]));
  add_1 add_1_4 (.A(A[0]), .B(B[0]), .C(1'b0), .out_4(add_1_4_out_4), .out_5(S[0]));
endmodule

module add_1 (
  input  A,
  input  B,
  input  C,
  output out_4,
  output out_5
);

  wire and_1_out, and_2_out, or_1_out, xor_1_out;

  xor xor_1 (xor_1_out, A, B);
  or or_1 (or_1_out, C, B);
  and and_1 (and_1_out, C, B);
  xor xor_2 (out_5, xor_1_out, C);
  and and_2 (and_2_out, or_1_out, A);
  or or_2 (out_4, and_2_out, and_1_out);
endmodule

module motor (
  input  Sensor_IR
);

  wire A___Betoneira_Local_out, acionamento_1_lampada, acionamento_1_motor, B___Betoneira_Remota_out;

  Button B___Betoneira_Remota (.out(B___Betoneira_Remota_out));
  Button A___Betoneira_Local (.out(A___Betoneira_Local_out));
  Acionamento acionamento_1 (
    .A(A___Betoneira_Local_out), .B(B___Betoneira_Remota_out), .C___Sensor_IR(Sensor_IR),
    .Lampada(acionamento_1_lampada), .Motor(acionamento_1_motor));
  LED Lampada (.in(acionamento_1_lampada));
  LED Motor (.in(acionamento_1_motor));
endmodule
