// Logisim project somador.circ as structural Verilog
module somador (
  input  A,
  input  B,
  input  C,
  output out_4,
  output out_5
);

  wire and_1_out, and_2_out, or_1_out, xor_1_out;

  xor xor_1 (xor_1_out, A, B);
  or or_1 (or_1_out, C, B);
  and and_1 (and_1_out, C, B);
  xor xor_2 (out_5, xor_1_out, C);
  and and_2 (and_2_out, or_1_out, A);
  or or_2 (out_4, and_2_out, and_1_out);
endmodule

module add_4 (
  input  [3:0] B,
  input  [3:0] A,
  output out_3,
  output [3:0] S
);

  wire somador_2_out_4, somador_3_out_4, somador_4_out_4;

  somador somador_1 (.A(A[3]), .B(B[3]), .C(somador_3_out_4), .out_4(out_3), .out_5(S[3]));
  somador somador_2 (.A(A[1]), .B(B[1]), .C(somador_4_out_4), .out_4(somador_2_out_4), .out_5(S[1]));
  somador somador_3 (.A(A[2]), .B(B[2]), .C(somador_2_out_4), .out_4(somador_3_out_4), .out_5(S[2]));
  somador somador_4 (.A(A[0]), .B(B[0]), .C(1'b0), .out_4(somador_4_out_4), .out_5(S[0]));
endmodule
